# Fritzing sketch minor (saved by Fritzing 0.9.3b)
breadboards: 1

parts:
  U2 = NodeMCU V1.0
  Part2 = Soil Moisture Sensor
  DHT1 = DHT11 Humitidy and Temperature Sensor
  M1 = DC Motor
  S1 = SWITCH-MOMENTARY-2 [package=tactile-pth-12mm]

nets:
  N1: U2.D4, DHT1.NULL
  GND: U2.GND, Part2.GND, DHT1.GND, M1.pin_2
  N2: U2.D5, M1.pin_1
  N3: U2.D6, S1.1
  VCC: U2.SD3, Part2.VCC, DHT1.VDD, S1.2
  N4: U2.A0, Part2.SIG

custom parts:
  NodeMCU V1.0: ESP8266 based NodeMCU
  DHT11 Humitidy and Temperature Sensor: DHT11 Humidity and Temperature Sensor
